// Logisim project hamil.circ as structural Verilog: 1 circuit, main circuit main
module main (
  input  D,
  input  C,
  input  B,
  input  A,
  output S0,
  output S1,
  output S2,
  output S3
);

  wire and_1_out, and_2_out, and_3_out, and_4_out, and_5_out, and_6_out, and_7_out, and_8_out, and_9_out,
       and_10_out, not_1_out, not_2_out, not_3_out, or_1_out, or_2_out, or_3_out, or_4_out;

  not not_1 (not_1_out, D);
  not not_2 (not_2_out, B);
  not not_3 (not_3_out, C);
  not not_4 (S0, A);
  and and_1 (and_1_out, not_2_out, A);
  and and_2 (and_2_out, B, S0);
  and and_3 (and_3_out, C, B);
  or or_1 (or_1_out, not_2_out, S0);
  and and_4 (and_4_out, A, B);
  or or_2 (or_2_out, S0, not_2_out);
  and and_5 (and_5_out, not_3_out, D);
  or or_3 (or_3_out, and_1_out, and_2_out);
  and and_6 (and_6_out, and_3_out, A);
  and and_7 (and_7_out, or_1_out, not_3_out);
  or or_4 (or_4_out, and_4_out, C);
  and and_8 (and_8_out, or_2_out, and_5_out);
  and and_9 (and_9_out, or_3_out, not_1_out);
  or or_5 (S2, and_6_out, and_7_out);
  and and_10 (and_10_out, or_4_out, not_1_out);
  or or_6 (S1, and_9_out, D);
  or or_7 (S3, and_10_out, and_8_out);
endmodule
