// Logisim project JamilInverso.circ as structural Verilog: 1 circuit, main circuit main
module main (
  input  D7,
  input  D6,
  input  D5,
  input  P4,
  input  D3,
  input  P2,
  input  P1,
  output C4,
  output C2,
  output C1,
  output D7c,
  output D6c,
  output D5c,
  output D3c,
  output D6c_2,
  output D6c_3,
  output D6c_4,
  output D6c_5
);

  wire and_1_out, and_2_out, and_3_out, and_4_out, and_5_out, and_6_out, and_7_out, and_8_out, and_9_out,
       and_10_out, and_11_out, and_12_out, and_13_out, and_14_out, and_15_out, and_16_out, and_17_out,
       and_18_out, and_19_out, and_20_out, and_21_out, and_22_out, and_23_out, and_24_out, and_25_out,
       and_26_out, and_27_out, and_28_out, and_29_out, and_30_out, and_31_out, and_32_out, and_33_out,
       not_1_out, not_2_out, not_3_out, not_4_out, not_5_out, not_6_out, not_7_out, not_8_out, not_9_out,
       not_10_out, not_11_out, not_12_out, not_13_out, not_14_out, not_15_out, not_16_out, not_17_out,
       or_1_out, or_2_out, or_3_out, or_4_out, or_5_out, or_6_out, or_7_out, or_8_out, or_13_out, or_14_out,
       or_15_out, xor_1_out, xor_2_out, xor_3_out, xor_4_out, xor_5_out;

  not not_1 (not_1_out, D7);
  not not_2 (not_2_out, D6);
  not not_3 (not_3_out, P4);
  not not_4 (not_4_out, D5);
  not not_5 (not_5_out, D3);
  not not_6 (not_6_out, P2);
  not not_7 (not_7_out, P1);
  xor xor_1 (xor_1_out, D6, D7);
  xor xor_2 (xor_2_out, D3, D5);
  xor xor_3 (xor_3_out, D5, xor_1_out);
  xor xor_4 (xor_4_out, xor_1_out, D3);
  xor xor_5 (xor_5_out, xor_2_out, D7);
  xor xor_6 (C4, P4, xor_3_out);
  xor xor_7 (C2, xor_4_out, P2);
  xor xor_8 (C1, xor_5_out, P1);
  not not_8 (not_8_out, D7);
  not not_9 (not_9_out, C4);
  not not_10 (not_10_out, D6);
  not not_11 (not_11_out, D5);
  not not_12 (not_12_out, D3);
  not not_13 (not_13_out, C2);
  not not_14 (not_14_out, C1);
  and and_1 (and_1_out, not_8_out, C4);
  and and_2 (and_2_out, and_1_out, and_3_out);
  and and_3 (and_3_out, C2, C1);
  and and_4 (and_4_out, D7, not_9_out);
  and and_5 (and_5_out, D7, not_13_out);
  and and_6 (and_6_out, D7, not_14_out);
  and and_7 (and_7_out, not_10_out, C4);
  and and_8 (and_8_out, and_7_out, and_9_out);
  and and_9 (and_9_out, C2, C1);
  and and_10 (and_10_out, D6, not_9_out);
  and and_11 (and_11_out, D6, not_13_out);
  and and_12 (and_12_out, D6, C1);
  and and_13 (and_13_out, not_11_out, C4);
  and and_14 (and_14_out, and_13_out, and_15_out);
  and and_15 (and_15_out, not_13_out, C1);
  and and_16 (and_16_out, D5, not_9_out);
  and and_17 (and_17_out, D5, C2);
  and and_18 (and_18_out, D5, not_14_out);
  and and_19 (and_19_out, not_12_out, not_9_out);
  and and_20 (and_20_out, and_19_out, and_21_out);
  and and_21 (and_21_out, C2, C1);
  and and_22 (and_22_out, D3, C4);
  and and_23 (and_23_out, D3, not_13_out);
  and and_24 (and_24_out, D3, not_14_out);
  or or_1 (or_1_out, and_2_out, and_4_out);
  or or_2 (or_2_out, and_8_out, and_10_out);
  or or_3 (or_3_out, and_14_out, and_16_out);
  or or_4 (or_4_out, and_20_out, and_22_out);
  or or_5 (or_5_out, or_1_out, and_5_out);
  or or_6 (or_6_out, or_2_out, and_11_out);
  or or_7 (or_7_out, or_3_out, and_17_out);
  or or_8 (or_8_out, or_4_out, and_23_out);
  or or_9 (D7c, or_5_out, and_6_out);
  or or_10 (D6c, or_6_out, and_12_out);
  or or_11 (D5c, or_7_out, and_18_out);
  or or_12 (D3c, or_8_out, and_24_out);
  not not_15 (not_15_out, D7c);
  not not_16 (not_16_out, D6c);
  not not_17 (not_17_out, D5c);
  not not_18 (D6c_5, D3c);
  and and_25 (and_25_out, D7c, D6c);
  or or_13 (or_13_out, D5c, D5c);
  and and_26 (and_26_out, not_17_out, D6c_5);
  and and_27 (and_27_out, D6c, not_17_out);
  or or_14 (or_14_out, D3c, D5c);
  and and_28 (and_28_out, not_17_out, D6c_5);
  and and_29 (and_29_out, D5c, D3c);
  and and_30 (and_30_out, and_25_out, or_13_out);
  or or_15 (or_15_out, and_26_out, not_16_out);
  and and_31 (and_31_out, and_27_out, D6c_5);
  and and_32 (and_32_out, or_14_out, not_16_out);
  or or_16 (D6c_4, and_28_out, and_29_out);
  and and_33 (and_33_out, or_15_out, not_15_out);
  or or_17 (D6c_3, and_31_out, and_32_out);
  or or_18 (D6c_2, and_30_out, and_33_out);

  // Notes on the sheet:
  //   C4
  //   D7
  //   C
  //   D
  //   C4
  //   D6
  //   D
  //   C
  //   C4
  //   D5
  //   D
  //   C
  //   C4
  //   D3
  //   D
  //   C
  //   C2
  //   B
  //   C1
  //   C2
  //   B
  //   A
  //   C2
  //   C1
  //   B
  //   A
  //   C2
  //   C1
  //   B
  //   A
  //   C1
  //   A
  //   D=D7, C=C4, B=C2, A=C1
  //   D
  //   C
  //   B
  //   A
endmodule
