// Logisim project multi.circ as structural Verilog: 1 circuit, main circuit main
module main (
  input  [3:0] C,
  input  I,
  input  [3:0] B,
  input  in_4,
  output Guardar,
  output Clear,
  output S0,
  output S1,
  output [5:0] out_9,
  output [7:0] out_10,
  output [7:0] out_11,
  output [7:0] Resultado,
  output [7:0] out_13,
  output [3:0] Edo_actual,
  output [3:0] Edo_sig
);

  wire clock_1_out, not_1_out, not_2_out;

  Multiplexer #(.select(3)) multiplexer_1 (
    .in0(1'b0), .in1(1'b0), .in2(B[0]), .in3(1'b0), .in4(1'b0), .in5(B[1]), .in6(1'b0), .in7(1'b0),
    .out(out_9[4]), .sel(Edo_actual[2:0]), .en(not_1_out));
  not not_1 (not_1_out, Edo_actual[3]);
  Multiplexer #(.select(3)) multiplexer_2 (
    .in0(B[2]), .in1(1'b0), .in2(1'b0), .in3(B[3]), .in4(1'b0), .out(out_9[4]), .sel(Edo_actual[2:0]),
    .en(Edo_actual[3]));  // open: in5, in6, in7
  ROM #(.addrWidth(6)) rom_1 (
    .addr({I, out_9[4], Edo_actual}), .data({Edo_sig, Guardar, Clear, out_10[1:0]}));  // open: sel
  Clock clock_1 (.out(clock_1_out));
  D_Flip_Flop d_ff_1 (.clk(clock_1_out), .D(Edo_sig[0]), .Q(Edo_actual[0]));  // open: Qn, preset, en, reset
  D_Flip_Flop d_ff_2 (.clk(clock_1_out), .D(Edo_sig[1]), .Q(Edo_actual[1]));  // open: Qn, preset, en, reset
  D_Flip_Flop d_ff_3 (.clk(clock_1_out), .D(Edo_sig[2]), .Q(Edo_actual[2]));  // open: Qn, preset, en, reset
  D_Flip_Flop d_ff_4 (.clk(clock_1_out), .D(Edo_sig[3]), .Q(Edo_actual[3]));  // open: Qn, preset, en, reset
  Shift_Register shift_register_1 (
    .shift(out_10[0]), .in(1'b0), .clk(clock_1_out), .load(out_10[1]), .clr(in_4), .d0(C[0]), .q0(out_11[0]),
    .d1(C[1]), .q1(out_11[1]), .d2(C[2]), .q2(out_11[2]), .d3(C[3]), .q3(out_11[3]), .d4(1'b0),
    .q4(out_11[4]), .d5(1'b0), .q5(out_11[5]), .d6(1'b0), .q6(out_11[6]), .d7(1'b0), .q7(out_11[7]));  // open: out
  not not_2 (not_2_out, Clear);
  Register register_1 (.D(out_13), .en(Guardar), .Q(Resultado), .clk(clock_1_out), .clr(not_2_out));
  Adder adder_1 (.a(out_11), .b(Resultado), .out(out_13));  // open: cin, cout

  assign {out_9[5], out_9[3:0]} = {I, Edo_actual};
  assign out_10[7:2] = {Edo_sig, Guardar, Clear};
  assign S0 = out_10[1];
  assign S1 = out_10[0];

  // Notes on the sheet:
  //   contents of rom_1 (hex, n*v repeats v):
  //   4 22 34 55 3c 64 85 6c 94 b5 9c c4 5 cc 0 0 4 22 44 55 3c 74 85 6c a4 b5 9c d4 5 cc 0 0 14 22 34 55
  //   3c 64 85 6c 94 b5 9c c4 5 cc 0 0 14 22 44 55 3c 74 85 6c a4 b5 9c d4 5 cc
endmodule
