// Logisim project ToposExamen3.circ as structural Verilog: 1 circuit, main circuit main
module main (
  input  in_1,
  input  [2:0] in_2,
  output [3:0] X,
  output [3:0] out_4,
  output Ya,
  output Yb,
  output Xa,
  output Xb,
  output [3:0] Puntuacion,
  output [3:0] _3_2_1_0,
  output Limite_Puntuacion,
  output [2:0] Salidas,
  output [3:0] Entradas,
  output [2:0] Edo__Siguiente,
  output [5:0] out_15,
  output [2:0] Edo__Actual,
  output [2:0] Edo__Falso,
  output [3:0] out_18,
  output Ya_2,
  output Yb_2,
  output Xa_2,
  output Xb_2,
  output [3:0] _0_1_2_3,
  output [3:0] _0_1_2_3_2
);

  wire _0_2_out, _0_out, _1_2_out, _1_out, _2_2_out, _2_out, _3_2_out, _3_out, _4_2_out, _4_out, _5_2_out,
       _5_out, _6_2_out, _6_out, _7_2_out, _7_out, _8_2_out, _8_out, _9_2_out, _9_out, _10_2_out, _10_out,
       _11_2_out, _11_out, _12_2_out, _12_out, _13_2_out, _13_out, _14_2_out, _14_out, _15_2_out, _15_out,
       and_1_out, and_2_out, and_3_out, and_4_out, and_6_out, and_7_out, and_8_out, and_9_out, and_10_out,
       and_11_out, and_12_out, and_13_out, and_14_out, and_15_out, and_16_out, and_17_out, and_18_out,
       and_19_out, and_20_out, and_21_out, and_22_out, and_23_out, and_24_out, and_25_out, and_26_out,
       and_27_out, and_28_out, and_29_out, and_30_out, and_31_out, and_32_out, and_33_out, clock_1_out,
       clock_2_out, clock_3_out, clock_4_out, clock_5_out, clock_6_out, comparator_1_eq, d_ff_1_q, d_ff_2_q,
       d_ff_3_q, d_ff_4_q, d_ff_5_q, d_ff_6_q, d_ff_7_q, d_ff_8_q, d_ff_9_q, d_ff_10_q, d_ff_11_q, d_ff_12_q,
       d_ff_13_q, d_ff_14_q, d_ff_15_q, d_ff_16_q, d_ff_17_q, d_ff_18_q, d_ff_19_q, d_ff_20_q, d_ff_21_q,
       d_ff_22_q, d_ff_23_q, d_ff_24_q, d_ff_25_q, d_ff_26_q, d_ff_27_q, d_ff_28_q, d_ff_29_q, d_ff_30_q,
       d_ff_31_q, d_ff_32_q, d_ff_33_q, d_ff_34_q, d_ff_35_q, d_ff_36_q, d_ff_37_q, d_ff_38_q, d_ff_39_q,
       d_ff_40_q, d_ff_41_q, d_ff_42_q, d_ff_43_q, d_ff_44_q, d_ff_45_q, d_ff_46_q, d_ff_47_q, d_ff_48_q,
       d_ff_49_q, d_ff_50_q, d_ff_51_q, d_ff_52_q, d_ff_53_q, d_ff_54_q, d_ff_55_q, d_ff_56_q, d_ff_57_q,
       d_ff_58_q, d_ff_59_q, d_ff_60_q, d_ff_61_q, d_ff_62_q, d_ff_63_q, d_ff_64_q, d_ff_65_q, d_ff_66_q,
       d_ff_67_q, d_ff_68_q, d_ff_69_q, d_ff_70_q, d_ff_71_q, d_ff_72_q, d_ff_73_q, d_ff_74_q, d_ff_75_q,
       d_ff_76_q, d_ff_77_q, d_ff_78_q, d_ff_79_q, d_ff_80_q, d_ff_81_q, d_ff_82_q, d_ff_83_q, d_ff_84_q,
       d_ff_85_q, d_ff_86_q, d_ff_86_qn, d_ff_87_q, d_ff_88_q, d_ff_88_qn, d_ff_89_q, d_ff_89_qn, d_ff_90_q,
       d_ff_91_q, d_ff_91_qn, d_ff_92_q, d_ff_93_q, d_ff_93_qn, d_ff_94_q, d_ff_95_q, d_ff_96_q, d_ff_96_qn,
       d_ff_97_q, d_ff_98_q, d_ff_98_qn, d_ff_99_q, d_ff_99_qn, d_ff_100_q, decoder_1_out0, decoder_1_out1,
       decoder_1_out2, decoder_1_out3, decoder_3_out0, decoder_3_out1, decoder_3_out2, decoder_3_out3,
       multiplexer_1_out, not_9_out, not_10_out, not_11_out, not_12_out, not_13_out, not_14_out, not_15_out,
       not_16_out, not_17_out, not_18_out, not_19_out, not_20_out, not_21_out, not_22_out, not_23_out,
       not_24_out, not_25_out, not_26_out, not_27_out, not_28_out, not_29_out, not_30_out, not_31_out,
       not_32_out, not_33_out, not_34_out, not_35_out, not_36_out, not_37_out, not_38_out, not_39_out,
       not_40_out, not_41_out, not_42_out, not_43_out, or_1_out, or_2_out, or_3_out, or_4_out, or_5_out,
       or_6_out, or_7_out, or_8_out, or_9_out, or_10_out, or_11_out, or_12_out, or_13_out, or_14_out,
       or_15_out;

  Clock clock_1 (.out(clock_1_out));
  LED Algun_boton_presionado (.in(or_5_out));
  Clock clock_2 (.out(clock_2_out));
  Random #(.width(4)) random_1 (.clk(clock_1_out), .next(out_15[0]), .out(out_4));  // open: clr
  Counter #(.width(4), .max('hf)) counter_1 (
    .count(not_41_out), .Q(out_18), .clk(clock_2_out));  // open: load, D, carry, clr
  Decoder #(.select(2)) decoder_1 (
    .out0(decoder_1_out0), .out1(decoder_1_out1), .out2(decoder_1_out2), .out3(decoder_1_out3),
    .sel(out_18[1:0]));  // open: en
  Decoder #(.select(2), .disabled(0)) decoder_2 (
    .out0(_0_1_2_3_2[3]), .out1(_0_1_2_3_2[2]), .out2(_0_1_2_3_2[1]), .out3(_0_1_2_3_2[0]), .sel(out_18[3:2]));  // open: en
  Decoder #(.select(2)) decoder_3 (
    .out0(decoder_3_out0), .out1(decoder_3_out1), .out2(decoder_3_out2), .out3(decoder_3_out3),
    .sel(out_4[1:0]));  // open: en
  Decoder #(.select(2), .disabled(0)) decoder_4 (
    .out0(_3_2_1_0[0]), .out1(_3_2_1_0[1]), .out2(_3_2_1_0[2]), .out3(_3_2_1_0[3]), .sel(out_4[3:2]),
    .en(Entradas[1]));
  not not_1 (_0_1_2_3[3], decoder_1_out0);
  not not_2 (_0_1_2_3[2], decoder_1_out1);
  not not_3 (_0_1_2_3[1], decoder_1_out2);
  not not_4 (_0_1_2_3[0], decoder_1_out3);
  not not_5 (X[0], decoder_3_out0);
  not not_6 (X[1], decoder_3_out1);
  not not_7 (X[2], decoder_3_out2);
  not not_8 (X[3], decoder_3_out3);
  Comparator #(.width(4)) comparator_1 (.a(out_4), .b(out_18), .eq(comparator_1_eq));  // open: gt, lt
  and _0 (_0_out, _3_2_1_0[0], not_9_out);
  not not_9 (not_9_out, X[0]);
  and _4 (_4_out, _3_2_1_0[1], not_10_out);
  not not_10 (not_10_out, X[0]);
  and _8 (_8_out, _3_2_1_0[2], not_11_out);
  not not_11 (not_11_out, X[0]);
  and _12 (_12_out, _3_2_1_0[3], not_12_out);
  not not_12 (not_12_out, X[0]);
  LED led_1 (.in(and_1_out));
  Button _0_2 (.out(_0_2_out));
  LED led_2 (.in(and_2_out));
  Button _4_2 (.out(_4_2_out));
  LED led_3 (.in(and_3_out));
  Button _8_2 (.out(_8_2_out));
  LED led_4 (.in(and_4_out));
  Button _12_2 (.out(_12_2_out));
  and and_1 (and_1_out, _0_1_2_3_2[3], not_13_out);
  not not_13 (not_13_out, _0_1_2_3[3]);
  and and_2 (and_2_out, _0_1_2_3_2[2], not_14_out);
  not not_14 (not_14_out, _0_1_2_3[3]);
  and and_3 (and_3_out, _0_1_2_3_2[1], not_15_out);
  not not_15 (not_15_out, _0_1_2_3[3]);
  and and_4 (and_4_out, _0_1_2_3_2[0], not_16_out);
  not not_16 (not_16_out, _0_1_2_3[3]);
  not not_17 (not_17_out, X[1]);
  LED led_5 (.in(_0_out));
  LED led_6 (.in(_0_out));
  LED led_7 (.in(_0_out));
  LED led_8 (.in(_0_out));
  not not_18 (not_18_out, X[1]);
  LED led_9 (.in(_4_out));
  LED led_10 (.in(_4_out));
  LED led_11 (.in(_4_out));
  LED led_12 (.in(_4_out));
  not not_19 (not_19_out, X[1]);
  LED led_13 (.in(_8_out));
  LED led_14 (.in(_8_out));
  LED led_15 (.in(_8_out));
  LED led_16 (.in(_8_out));
  not not_20 (not_20_out, X[1]);
  LED led_17 (.in(_12_out));
  LED led_18 (.in(_12_out));
  LED led_19 (.in(_12_out));
  LED led_20 (.in(_12_out));
  LED Atinar (.in(Entradas[0]));
  and and_5 (Entradas[0], comparator_1_eq, or_5_out);
  and and_6 (and_6_out, and_1_out, _0_2_out);
  and and_7 (and_7_out, and_2_out, _4_2_out);
  and and_8 (and_8_out, and_3_out, _8_2_out);
  and and_9 (and_9_out, and_4_out, _12_2_out);
  not not_21 (not_21_out, _0_1_2_3[2]);
  not not_22 (not_22_out, _0_1_2_3[2]);
  not not_23 (not_23_out, _0_1_2_3[2]);
  not not_24 (not_24_out, _0_1_2_3[2]);
  and _1 (_1_out, _3_2_1_0[0], not_17_out);
  LED led_21 (.in(_1_out));
  LED led_22 (.in(_1_out));
  LED led_23 (.in(_1_out));
  LED led_24 (.in(_1_out));
  and _5 (_5_out, _3_2_1_0[1], not_18_out);
  LED led_25 (.in(_5_out));
  LED led_26 (.in(_5_out));
  LED led_27 (.in(_5_out));
  LED led_28 (.in(_5_out));
  and _9 (_9_out, _3_2_1_0[2], not_19_out);
  LED led_29 (.in(_9_out));
  LED led_30 (.in(_9_out));
  LED led_31 (.in(_9_out));
  LED led_32 (.in(_9_out));
  and _13 (_13_out, _3_2_1_0[3], not_20_out);
  LED led_33 (.in(_13_out));
  LED led_34 (.in(_13_out));
  LED led_35 (.in(_13_out));
  LED led_36 (.in(_13_out));
  LED led_37 (.in(and_13_out));
  and and_10 (and_10_out, and_13_out, _1_2_out);
  Button _1_2 (.out(_1_2_out));
  LED led_38 (.in(and_14_out));
  and and_11 (and_11_out, and_14_out, _5_2_out);
  Button _5_2 (.out(_5_2_out));
  LED led_39 (.in(and_15_out));
  and and_12 (and_12_out, and_15_out, _9_2_out);
  Button _9_2 (.out(_9_2_out));
  LED led_40 (.in(and_16_out));
  Button _13_2 (.out(_13_2_out));
  and and_13 (and_13_out, _0_1_2_3_2[3], not_21_out);
  and and_14 (and_14_out, _0_1_2_3_2[2], not_22_out);
  and and_15 (and_15_out, _0_1_2_3_2[1], not_23_out);
  and and_16 (and_16_out, _0_1_2_3_2[0], not_24_out);
  and _2 (_2_out, _3_2_1_0[0], not_25_out);
  not not_25 (not_25_out, X[2]);
  LED led_41 (.in(_2_out));
  LED led_42 (.in(_2_out));
  LED led_43 (.in(_2_out));
  LED led_44 (.in(_2_out));
  and _6 (_6_out, _3_2_1_0[1], not_26_out);
  not not_26 (not_26_out, X[2]);
  LED led_45 (.in(_6_out));
  LED led_46 (.in(_6_out));
  LED led_47 (.in(_6_out));
  LED led_48 (.in(_6_out));
  and _10 (_10_out, _3_2_1_0[2], not_27_out);
  not not_27 (not_27_out, X[2]);
  LED led_49 (.in(_10_out));
  LED led_50 (.in(_10_out));
  LED led_51 (.in(_10_out));
  LED led_52 (.in(_10_out));
  and _14 (_14_out, _3_2_1_0[3], not_28_out);
  not not_28 (not_28_out, X[2]);
  LED led_53 (.in(_14_out));
  LED led_54 (.in(_14_out));
  LED led_55 (.in(_14_out));
  LED led_56 (.in(_14_out));
  LED led_57 (.in(and_18_out));
  Button _2_2 (.out(_2_2_out));
  LED led_58 (.in(and_19_out));
  Button _6_2 (.out(_6_2_out));
  LED led_59 (.in(and_20_out));
  Button _10_2 (.out(_10_2_out));
  LED led_60 (.in(and_21_out));
  and and_17 (and_17_out, and_16_out, _13_2_out);
  Button _14_2 (.out(_14_2_out));
  and and_18 (and_18_out, _0_1_2_3_2[3], not_29_out);
  not not_29 (not_29_out, _0_1_2_3[1]);
  and and_19 (and_19_out, _0_1_2_3_2[2], not_30_out);
  not not_30 (not_30_out, _0_1_2_3[1]);
  and and_20 (and_20_out, _0_1_2_3_2[1], not_31_out);
  not not_31 (not_31_out, _0_1_2_3[1]);
  and and_21 (and_21_out, _0_1_2_3_2[0], not_32_out);
  not not_32 (not_32_out, _0_1_2_3[1]);
  and _3 (_3_out, _3_2_1_0[0], not_33_out);
  not not_33 (not_33_out, X[3]);
  LED led_61 (.in(_3_out));
  LED led_62 (.in(_3_out));
  LED led_63 (.in(_3_out));
  LED led_64 (.in(_3_out));
  and _7 (_7_out, _3_2_1_0[1], not_34_out);
  not not_34 (not_34_out, X[3]);
  LED led_65 (.in(_7_out));
  LED led_66 (.in(_7_out));
  LED led_67 (.in(_7_out));
  LED led_68 (.in(_7_out));
  and _11 (_11_out, _3_2_1_0[2], not_35_out);
  not not_35 (not_35_out, X[3]);
  LED led_69 (.in(_11_out));
  LED led_70 (.in(_11_out));
  LED led_71 (.in(_11_out));
  LED led_72 (.in(_11_out));
  and _15 (_15_out, _3_2_1_0[3], not_36_out);
  not not_36 (not_36_out, X[3]);
  LED led_73 (.in(_15_out));
  LED led_74 (.in(_15_out));
  LED led_75 (.in(_15_out));
  LED led_76 (.in(_15_out));
  LED led_77 (.in(and_26_out));
  and and_22 (and_22_out, and_18_out, _2_2_out);
  Button _3_2 (.out(_3_2_out));
  LED led_78 (.in(and_27_out));
  and and_23 (and_23_out, and_19_out, _6_2_out);
  Button _7_2 (.out(_7_2_out));
  LED led_79 (.in(and_28_out));
  and and_24 (and_24_out, and_20_out, _10_2_out);
  Button _11_2 (.out(_11_2_out));
  LED led_80 (.in(and_29_out));
  and and_25 (and_25_out, and_21_out, _14_2_out);
  Button _15_2 (.out(_15_2_out));
  and and_26 (and_26_out, _0_1_2_3_2[3], not_37_out);
  not not_37 (not_37_out, _0_1_2_3[0]);
  and and_27 (and_27_out, _0_1_2_3_2[2], not_38_out);
  not not_38 (not_38_out, _0_1_2_3[0]);
  and and_28 (and_28_out, _0_1_2_3_2[1], not_39_out);
  not not_39 (not_39_out, _0_1_2_3[0]);
  and and_29 (and_29_out, _0_1_2_3_2[0], not_40_out);
  not not_40 (not_40_out, _0_1_2_3[0]);
  not not_41 (not_41_out, or_5_out);
  and and_30 (and_30_out, and_26_out, _3_2_out);
  and and_31 (and_31_out, and_27_out, _7_2_out);
  and and_32 (and_32_out, and_28_out, _11_2_out);
  and and_33 (and_33_out, and_29_out, _15_2_out);
  or or_1 (or_1_out, and_30_out, and_22_out, and_10_out, and_6_out);
  or or_2 (or_2_out, and_31_out, and_23_out, and_11_out, and_7_out);
  or or_3 (or_3_out, and_32_out, and_24_out, and_12_out, and_8_out);
  or or_4 (or_4_out, and_33_out, and_25_out, and_17_out, and_9_out);
  Counter #(.width(4), .max('hf)) counter_2 (
    .count(out_15[1]), .Q(Puntuacion), .carry(Entradas[2]), .clk(clock_3_out), .clr(out_15[2]));  // open: load, D
  Clock clock_3 (.out(clock_3_out));
  Button Inicio (.out(Entradas[3]));
  or or_5 (or_5_out, or_4_out, or_3_out, or_2_out, or_1_out);
  LED led_81 (.in(Puntuacion[2]));
  LED led_82 (.in(Puntuacion[1]));
  LED led_83 (.in(Puntuacion[3]));
  LED led_84 (.in(Puntuacion[0]));
  Clock clock_4 (.out(clock_4_out));
  Counter #(.width(3), .max('h7)) counter_3 (.load(in_1), .D(in_2), .clk(clock_5_out));  // open: count, Q, carry, clr
  Clock clock_5 (.out(clock_5_out));
  not not_42 (not_42_out, Entradas[2]);
  D_Flip_Flop d_ff_1 (.clk(clock_4_out), .D(out_15[0]), .Q(d_ff_1_q));  // open: Qn, preset, en, reset
  D_Flip_Flop d_ff_2 (.clk(clock_4_out), .D(d_ff_84_q), .Q(d_ff_2_q));  // open: Qn, preset, en, reset
  D_Flip_Flop d_ff_3 (.clk(clock_4_out), .D(d_ff_85_q), .Q(d_ff_3_q));  // open: Qn, preset, en, reset
  Multiplexer #(.select(3)) multiplexer_1 (
    .in0(Entradas[3]), .in1(1'b1), .in2(not_42_out), .in3(Entradas[1]), .in4(Entradas[0]), .in5(1'b0),
    .in6(1'b1), .in7(1'b1), .out(multiplexer_1_out), .sel(Edo__Actual));  // open: en
  D_Flip_Flop d_ff_4 (.clk(clock_4_out), .D(d_ff_1_q), .Q(d_ff_4_q));  // open: Qn, preset, en, reset
  D_Flip_Flop d_ff_5 (.clk(clock_4_out), .D(d_ff_2_q), .Q(d_ff_5_q));  // open: Qn, preset, en, reset
  D_Flip_Flop d_ff_6 (.clk(clock_4_out), .D(d_ff_3_q), .Q(d_ff_6_q));  // open: Qn, preset, en, reset
  D_Flip_Flop d_ff_7 (.clk(clock_4_out), .D(d_ff_86_q), .Q(d_ff_7_q));  // open: Qn, preset, en, reset
  D_Flip_Flop d_ff_8 (.clk(clock_4_out), .D(d_ff_7_q), .Q(d_ff_8_q));  // open: Qn, preset, en, reset
  D_Flip_Flop d_ff_9 (.clk(clock_4_out), .D(d_ff_10_q), .Q(d_ff_9_q));  // open: Qn, preset, en, reset
  D_Flip_Flop d_ff_10 (.clk(clock_4_out), .D(d_ff_88_q), .Q(d_ff_10_q));  // open: Qn, preset, en, reset
  D_Flip_Flop d_ff_11 (.clk(clock_4_out), .D(d_ff_12_q), .Q(d_ff_11_q));  // open: Qn, preset, en, reset
  D_Flip_Flop d_ff_12 (.clk(clock_4_out), .D(d_ff_89_q), .Q(d_ff_12_q));  // open: Qn, preset, en, reset
  D_Flip_Flop d_ff_13 (.clk(clock_4_out), .D(or_11_out), .Q(d_ff_13_q));  // open: Qn, preset, en, reset
  D_Flip_Flop d_ff_14 (.clk(clock_4_out), .D(d_ff_13_q), .Q(d_ff_14_q));  // open: Qn, preset, en, reset
  D_Flip_Flop d_ff_15 (.clk(clock_4_out), .D(d_ff_93_q), .Q(d_ff_15_q));  // open: Qn, preset, en, reset
  D_Flip_Flop d_ff_16 (.clk(clock_4_out), .D(d_ff_15_q), .Q(d_ff_16_q));  // open: Qn, preset, en, reset
  D_Flip_Flop d_ff_17 (.clk(clock_4_out), .D(d_ff_18_q), .Q(d_ff_17_q));  // open: Qn, preset, en, reset
  D_Flip_Flop d_ff_18 (.clk(clock_4_out), .D(d_ff_96_q), .Q(d_ff_18_q));  // open: Qn, preset, en, reset
  D_Flip_Flop d_ff_19 (.clk(clock_4_out), .D(d_ff_98_q), .Q(d_ff_19_q));  // open: Qn, preset, en, reset
  D_Flip_Flop d_ff_20 (.clk(clock_4_out), .D(d_ff_19_q), .Q(d_ff_20_q));  // open: Qn, preset, en, reset
  not not_43 (not_43_out, multiplexer_1_out);
  Counter #(.width(3), .max('h7)) counter_4 (
    .load(not_43_out), .D(Edo__Falso), .count(multiplexer_1_out), .Q(Edo__Actual), .clk(clock_6_out));  // open: carry, clr
  Clock clock_6 (.out(clock_6_out));
  D_Flip_Flop d_ff_21 (.clk(clock_4_out), .D(d_ff_22_q), .Q(d_ff_21_q));  // open: Qn, preset, en, reset
  D_Flip_Flop d_ff_22 (.clk(clock_4_out), .D(d_ff_4_q), .Q(d_ff_22_q));  // open: Qn, preset, en, reset
  D_Flip_Flop d_ff_23 (.clk(clock_4_out), .D(d_ff_5_q), .Q(d_ff_23_q));  // open: Qn, preset, en, reset
  D_Flip_Flop d_ff_24 (.clk(clock_4_out), .D(d_ff_6_q), .Q(d_ff_24_q));  // open: Qn, preset, en, reset
  D_Flip_Flop d_ff_25 (.clk(clock_4_out), .D(d_ff_8_q), .Q(d_ff_25_q));  // open: Qn, preset, en, reset
  D_Flip_Flop d_ff_26 (.clk(clock_4_out), .D(d_ff_9_q), .Q(d_ff_26_q));  // open: Qn, preset, en, reset
  D_Flip_Flop d_ff_27 (.clk(clock_4_out), .D(d_ff_11_q), .Q(d_ff_27_q));  // open: Qn, preset, en, reset
  D_Flip_Flop d_ff_28 (.clk(clock_4_out), .D(d_ff_14_q), .Q(d_ff_28_q));  // open: Qn, preset, en, reset
  D_Flip_Flop d_ff_29 (.clk(clock_4_out), .D(d_ff_16_q), .Q(d_ff_29_q));  // open: Qn, preset, en, reset
  D_Flip_Flop d_ff_30 (.clk(clock_4_out), .D(d_ff_17_q), .Q(d_ff_30_q));  // open: Qn, preset, en, reset
  D_Flip_Flop d_ff_31 (.clk(clock_4_out), .D(d_ff_20_q), .Q(d_ff_31_q));  // open: Qn, preset, en, reset
  D_Flip_Flop d_ff_32 (.clk(clock_4_out), .D(d_ff_21_q), .Q(d_ff_32_q));  // open: Qn, preset, en, reset
  D_Flip_Flop d_ff_33 (.clk(clock_4_out), .D(d_ff_23_q), .Q(d_ff_33_q));  // open: Qn, preset, en, reset
  D_Flip_Flop d_ff_34 (.clk(clock_4_out), .D(d_ff_33_q), .Q(d_ff_34_q));  // open: Qn, preset, en, reset
  D_Flip_Flop d_ff_35 (.clk(clock_4_out), .D(d_ff_24_q), .Q(d_ff_35_q));  // open: Qn, preset, en, reset
  D_Flip_Flop d_ff_36 (.clk(clock_4_out), .D(d_ff_35_q), .Q(d_ff_36_q));  // open: Qn, preset, en, reset
  D_Flip_Flop d_ff_37 (.clk(clock_4_out), .D(d_ff_25_q), .Q(d_ff_37_q));  // open: Qn, preset, en, reset
  D_Flip_Flop d_ff_38 (.clk(clock_4_out), .D(d_ff_26_q), .Q(d_ff_38_q));  // open: Qn, preset, en, reset
  D_Flip_Flop d_ff_39 (.clk(clock_4_out), .D(d_ff_27_q), .Q(d_ff_39_q));  // open: Qn, preset, en, reset
  D_Flip_Flop d_ff_40 (.clk(clock_4_out), .D(d_ff_28_q), .Q(d_ff_40_q));  // open: Qn, preset, en, reset
  D_Flip_Flop d_ff_41 (.clk(clock_4_out), .D(d_ff_29_q), .Q(d_ff_41_q));  // open: Qn, preset, en, reset
  D_Flip_Flop d_ff_42 (.clk(clock_4_out), .D(d_ff_30_q), .Q(d_ff_42_q));  // open: Qn, preset, en, reset
  D_Flip_Flop d_ff_43 (.clk(clock_4_out), .D(d_ff_31_q), .Q(d_ff_43_q));  // open: Qn, preset, en, reset
  ROM #(.addrWidth(3), .dataWidth(6)) rom_1 (.addr(Edo__Actual), .data({Edo__Falso, out_15[2:0]}));  // open: sel
  D_Flip_Flop d_ff_44 (.clk(clock_4_out), .D(d_ff_32_q), .Q(d_ff_44_q));  // open: Qn, preset, en, reset
  or or_6 (or_6_out, d_ff_1_q, d_ff_4_q, d_ff_22_q, d_ff_21_q, d_ff_32_q, d_ff_44_q, d_ff_62_q, d_ff_61_q, d_ff_72_q, d_ff_84_q);
  D_Flip_Flop d_ff_45 (.clk(clock_4_out), .D(d_ff_34_q), .Q(d_ff_45_q));  // open: Qn, preset, en, reset
  or or_7 (or_7_out, d_ff_2_q, d_ff_5_q, d_ff_23_q, d_ff_33_q, d_ff_34_q, d_ff_45_q, d_ff_63_q, d_ff_74_q, d_ff_73_q, d_ff_85_q);
  D_Flip_Flop d_ff_46 (.clk(clock_4_out), .D(d_ff_36_q), .Q(d_ff_46_q));  // open: Qn, preset, en, reset
  or or_8 (or_8_out, d_ff_3_q, d_ff_6_q, d_ff_24_q, d_ff_35_q, d_ff_36_q, d_ff_46_q, d_ff_64_q, d_ff_76_q, d_ff_75_q, d_ff_86_q);
  D_Flip_Flop d_ff_47 (.clk(clock_4_out), .D(d_ff_37_q), .Q(d_ff_47_q));  // open: Qn, preset, en, reset
  D_Flip_Flop d_ff_48 (.clk(clock_4_out), .D(d_ff_47_q), .Q(d_ff_48_q));  // open: Qn, preset, en, reset
  or or_9 (or_9_out, d_ff_7_q, d_ff_8_q, d_ff_25_q, d_ff_37_q, d_ff_47_q, d_ff_48_q, d_ff_65_q, d_ff_77_q, d_ff_87_q, d_ff_88_q);
  D_Flip_Flop d_ff_49 (.clk(clock_4_out), .D(d_ff_50_q), .Q(d_ff_49_q));  // open: Qn, preset, en, reset
  D_Flip_Flop d_ff_50 (.clk(clock_4_out), .D(d_ff_38_q), .Q(d_ff_50_q));  // open: Qn, preset, en, reset
  or or_10 (or_10_out, d_ff_10_q, d_ff_9_q, d_ff_26_q, d_ff_38_q, d_ff_50_q, d_ff_49_q, d_ff_66_q, d_ff_78_q, d_ff_90_q, d_ff_89_q);
  D_Flip_Flop d_ff_51 (.clk(clock_4_out), .D(d_ff_39_q), .Q(d_ff_51_q));  // open: Qn, preset, en, reset
  D_Flip_Flop d_ff_52 (.clk(clock_4_out), .D(d_ff_51_q), .Q(d_ff_52_q));  // open: Qn, preset, en, reset
  or or_11 (or_11_out, d_ff_12_q, d_ff_11_q, d_ff_27_q, d_ff_39_q, d_ff_51_q, d_ff_52_q, d_ff_67_q, d_ff_79_q, d_ff_92_q, d_ff_91_q);
  D_Flip_Flop d_ff_53 (.clk(clock_4_out), .D(d_ff_40_q), .Q(d_ff_53_q));  // open: Qn, preset, en, reset
  D_Flip_Flop d_ff_54 (.clk(clock_4_out), .D(d_ff_53_q), .Q(d_ff_54_q));  // open: Qn, preset, en, reset
  or or_12 (or_12_out, d_ff_13_q, d_ff_14_q, d_ff_28_q, d_ff_40_q, d_ff_53_q, d_ff_54_q, d_ff_68_q, d_ff_80_q, d_ff_94_q, d_ff_93_q);
  D_Flip_Flop d_ff_55 (.clk(clock_4_out), .D(d_ff_41_q), .Q(d_ff_55_q));  // open: Qn, preset, en, reset
  D_Flip_Flop d_ff_56 (.clk(clock_4_out), .D(d_ff_55_q), .Q(d_ff_56_q));  // open: Qn, preset, en, reset
  or or_13 (or_13_out, d_ff_15_q, d_ff_16_q, d_ff_29_q, d_ff_41_q, d_ff_55_q, d_ff_56_q, d_ff_69_q, d_ff_81_q, d_ff_95_q, d_ff_96_q);
  D_Flip_Flop d_ff_57 (.clk(clock_4_out), .D(d_ff_42_q), .Q(d_ff_57_q));  // open: Qn, preset, en, reset
  D_Flip_Flop d_ff_58 (.clk(clock_4_out), .D(d_ff_57_q), .Q(d_ff_58_q));  // open: Qn, preset, en, reset
  or or_14 (or_14_out, d_ff_18_q, d_ff_17_q, d_ff_30_q, d_ff_42_q, d_ff_57_q, d_ff_58_q, d_ff_70_q, d_ff_82_q, d_ff_97_q, d_ff_98_q);
  D_Flip_Flop d_ff_59 (.clk(clock_4_out), .D(d_ff_43_q), .Q(d_ff_59_q));  // open: Qn, preset, en, reset
  D_Flip_Flop d_ff_60 (.clk(clock_4_out), .D(d_ff_59_q), .Q(d_ff_60_q));  // open: Qn, preset, en, reset
  or or_15 (or_15_out, d_ff_19_q, d_ff_20_q, d_ff_31_q, d_ff_43_q, d_ff_59_q, d_ff_60_q, d_ff_71_q, d_ff_83_q, d_ff_100_q, d_ff_99_q);
  D_Flip_Flop d_ff_61 (.clk(clock_4_out), .D(d_ff_62_q), .Q(d_ff_61_q));  // open: Qn, preset, en, reset
  D_Flip_Flop d_ff_62 (.clk(clock_4_out), .D(d_ff_44_q), .Q(d_ff_62_q));  // open: Qn, preset, en, reset
  D_Flip_Flop d_ff_63 (.clk(clock_4_out), .D(d_ff_45_q), .Q(d_ff_63_q));  // open: Qn, preset, en, reset
  D_Flip_Flop d_ff_64 (.clk(clock_4_out), .D(d_ff_46_q), .Q(d_ff_64_q));  // open: Qn, preset, en, reset
  D_Flip_Flop d_ff_65 (.clk(clock_4_out), .D(d_ff_48_q), .Q(d_ff_65_q));  // open: Qn, preset, en, reset
  D_Flip_Flop d_ff_66 (.clk(clock_4_out), .D(d_ff_49_q), .Q(d_ff_66_q));  // open: Qn, preset, en, reset
  D_Flip_Flop d_ff_67 (.clk(clock_4_out), .D(d_ff_52_q), .Q(d_ff_67_q));  // open: Qn, preset, en, reset
  D_Flip_Flop d_ff_68 (.clk(clock_4_out), .D(d_ff_54_q), .Q(d_ff_68_q));  // open: Qn, preset, en, reset
  D_Flip_Flop d_ff_69 (.clk(clock_4_out), .D(d_ff_56_q), .Q(d_ff_69_q));  // open: Qn, preset, en, reset
  D_Flip_Flop d_ff_70 (.clk(clock_4_out), .D(d_ff_58_q), .Q(d_ff_70_q));  // open: Qn, preset, en, reset
  D_Flip_Flop d_ff_71 (.clk(clock_4_out), .D(d_ff_60_q), .Q(d_ff_71_q));  // open: Qn, preset, en, reset
  D_Flip_Flop d_ff_72 (.clk(clock_4_out), .D(d_ff_61_q), .Q(d_ff_72_q));  // open: Qn, preset, en, reset
  D_Flip_Flop d_ff_73 (.clk(clock_4_out), .D(d_ff_74_q), .Q(d_ff_73_q));  // open: Qn, preset, en, reset
  D_Flip_Flop d_ff_74 (.clk(clock_4_out), .D(d_ff_63_q), .Q(d_ff_74_q));  // open: Qn, preset, en, reset
  D_Flip_Flop d_ff_75 (.clk(clock_4_out), .D(d_ff_76_q), .Q(d_ff_75_q));  // open: Qn, preset, en, reset
  D_Flip_Flop d_ff_76 (.clk(clock_4_out), .D(d_ff_64_q), .Q(d_ff_76_q));  // open: Qn, preset, en, reset
  D_Flip_Flop d_ff_77 (.clk(clock_4_out), .D(d_ff_65_q), .Q(d_ff_77_q));  // open: Qn, preset, en, reset
  D_Flip_Flop d_ff_78 (.clk(clock_4_out), .D(d_ff_66_q), .Q(d_ff_78_q));  // open: Qn, preset, en, reset
  D_Flip_Flop d_ff_79 (.clk(clock_4_out), .D(d_ff_67_q), .Q(d_ff_79_q));  // open: Qn, preset, en, reset
  D_Flip_Flop d_ff_80 (.clk(clock_4_out), .D(d_ff_68_q), .Q(d_ff_80_q));  // open: Qn, preset, en, reset
  D_Flip_Flop d_ff_81 (.clk(clock_4_out), .D(d_ff_69_q), .Q(d_ff_81_q));  // open: Qn, preset, en, reset
  D_Flip_Flop d_ff_82 (.clk(clock_4_out), .D(d_ff_70_q), .Q(d_ff_82_q));  // open: Qn, preset, en, reset
  D_Flip_Flop d_ff_83 (.clk(clock_4_out), .D(d_ff_71_q), .Q(d_ff_83_q));  // open: Qn, preset, en, reset
  D_Flip_Flop d_ff_84 (.clk(clock_4_out), .D(d_ff_72_q), .Q(d_ff_84_q));  // open: Qn, preset, en, reset
  D_Flip_Flop d_ff_85 (.clk(clock_4_out), .D(d_ff_73_q), .Q(d_ff_85_q));  // open: Qn, preset, en, reset
  D_Flip_Flop d_ff_86 (.clk(clock_4_out), .D(d_ff_75_q), .Q(d_ff_86_q), .Qn(d_ff_86_qn));  // open: preset, en, reset
  D_Flip_Flop d_ff_87 (.clk(clock_4_out), .D(d_ff_77_q), .Q(d_ff_87_q));  // open: Qn, preset, en, reset
  D_Flip_Flop d_ff_88 (.clk(clock_4_out), .D(d_ff_87_q), .Q(d_ff_88_q), .Qn(d_ff_88_qn));  // open: preset, en, reset
  D_Flip_Flop d_ff_89 (.clk(clock_4_out), .D(d_ff_90_q), .Q(d_ff_89_q), .Qn(d_ff_89_qn));  // open: preset, en, reset
  D_Flip_Flop d_ff_90 (.clk(clock_4_out), .D(d_ff_78_q), .Q(d_ff_90_q));  // open: Qn, preset, en, reset
  D_Flip_Flop d_ff_91 (.clk(clock_4_out), .D(d_ff_92_q), .Q(d_ff_91_q), .Qn(d_ff_91_qn));  // open: preset, en, reset
  D_Flip_Flop d_ff_92 (.clk(clock_4_out), .D(d_ff_79_q), .Q(d_ff_92_q));  // open: Qn, preset, en, reset
  D_Flip_Flop d_ff_93 (.clk(clock_4_out), .D(d_ff_94_q), .Q(d_ff_93_q), .Qn(d_ff_93_qn));  // open: preset, en, reset
  D_Flip_Flop d_ff_94 (.clk(clock_4_out), .D(d_ff_80_q), .Q(d_ff_94_q));  // open: Qn, preset, en, reset
  D_Flip_Flop d_ff_95 (.clk(clock_4_out), .D(d_ff_81_q), .Q(d_ff_95_q));  // open: Qn, preset, en, reset
  D_Flip_Flop d_ff_96 (.clk(clock_4_out), .D(d_ff_95_q), .Q(d_ff_96_q), .Qn(d_ff_96_qn));  // open: preset, en, reset
  D_Flip_Flop d_ff_97 (.clk(clock_4_out), .D(d_ff_82_q), .Q(d_ff_97_q));  // open: Qn, preset, en, reset
  D_Flip_Flop d_ff_98 (.clk(clock_4_out), .D(d_ff_97_q), .Q(d_ff_98_q), .Qn(d_ff_98_qn));  // open: preset, en, reset
  D_Flip_Flop d_ff_99 (.clk(clock_4_out), .D(d_ff_100_q), .Q(d_ff_99_q), .Qn(d_ff_99_qn));  // open: preset, en, reset
  D_Flip_Flop d_ff_100 (.clk(clock_4_out), .D(d_ff_83_q), .Q(d_ff_100_q));  // open: Qn, preset, en, reset
  or or_16 (Entradas[1], or_6_out, or_7_out, or_8_out, or_9_out, or_10_out, or_11_out, or_12_out, or_13_out, or_14_out, or_15_out);

  assign Edo__Siguiente = Edo__Falso;
  assign Limite_Puntuacion = Entradas[2];
  assign out_15[5:3] = Edo__Falso;
  assign Salidas = out_15[2:0];
  assign Xa = out_4[1];
  assign Xa_2 = out_18[1];
  assign Xb = out_4[0];
  assign Xb_2 = out_18[0];
  assign Ya = out_4[3];
  assign Ya_2 = out_18[3];
  assign Yb = out_4[2];
  assign Yb_2 = out_18[2];

  // Notes on the sheet:
  //   Simular a 64Hz
  //   LED seleccionado:
  //   Porfavor
  //   Cambien las cosas
  //   Muevan las cosas
  //   Renombren las cosas
  //   Renombren el archivo
  //   Por: Isuky Pohlo
  //   Boton presionado:
  //   X
  //   Y
  //   Y
  //   3 2 1 0
  //   X0
  //   Y0
  //   Y1
  //   Y2
  //   Y3
  //   X0
  //   X1
  //   X1
  //   X2
  //   X2
  //   X3
  //   X3
  //   Y0
  //   Y1
  //   Y2
  //   Y3
  //   Sumar
  //   Reseteo
  //   Maquina de estados:
  //   Entradas multiplexadas, salidas directas
  //   contents of rom_1 (hex, n*v repeats v):
  //   0 14 1 0 18 12
endmodule
